# Fritzing sketch SparkCoreBike (saved by Fritzing 0.8.7b)
circuit board: 8.03848cm x 3.69193cm
breadboards: 1

parts:
  U1 = Spark Core (v1.0)
  S1 = Reed switch [package=THT]
  R1 = Resistor [package="2010 [SMD]"]
  VCC1 = 4 x AAA Battery Mount
  LCD1 = LCD screen

nets:
  N1: U1.A2, U1.3V3
  N2: U1.A3, U1.A6
  VIN: U1.A5, U1.VIN, S1.pin_1, R1.Pin_1, VCC1.+, LCD1.VDD
  GND: U1.GND, R1.Pin_0, VCC1.-, LCD1.VSS
  N3: U1.D0, LCD1.RS
  N4: U1.D1, LCD1.R/W
  N5: U1.D2, LCD1.E
  N6: U1.D3, LCD1.DB4
  N7: U1.D4, LCD1.DB5
  N8: U1.D5, LCD1.DB6
  N9: U1.D6, LCD1.DB7
  N10: U1.3V3*, S1.pin_2

notes:
  Wheel rotation reed switch inside bike

custom parts:
  Spark Core (v1.0): The Spark Core is a tiny Wi-Fi development board that makes it easy to create internet-connected hardware. The Core is all you need to get started; power it over USB and in minutes you'll be controlling LEDs, switches and motors and collecting data from sensors over the internet! It has 8 digital I/O pins, 8 analog I/O pins, 8 PWM pins; UART (Serial), SPI, I2C, and JTAG peripherals available.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
